# Fritzing sketch routing (saved by Fritzing 0.9.3b)
circuit board: 8.46667cm x 5.64444cm

parts:
  U1 = NodeMCU V1.0
  RHT1 = Humidity and Temperature Sensor RHT03

nets:
  3V3: U1.3V3, RHT1.Vcc
  N1: U1.GND, RHT1.GND_2
  N2: U1.D5, RHT1.Data-signal

custom parts:
  NodeMCU V1.0: ESP8266 based NodeMCU
